# Fritzing sketch Untitled Sketch (saved by Fritzing 0.9.4)
breadboards: 1

parts:
  Компонент1 = Arduino Nano (Rev3.0)
  S1 = Pushbutton [package="[SMD]"]
  S2 = Pushbutton [package="[SMD]"]
  S3 = Pushbutton [package="[SMD]"]
  Q1 = NPN-Transistor [package="TO92 [THT]"]
  R1 = Resistor [tolerance=±5% resistance=22 package="2512 [SMD]"]
  R2 = Resistor [tolerance=±5% resistance=1k package="2512 [SMD]"]
  Part1 = KY-022 Infrared Receiver Module [package="Breakout board"]
  Display1 = LCD screen 16x2 IIC [part_number=101290]
  LED1 = Infrared LED - 5mm [package="5 mm [THT]"]  # not connected

nets:
  GND: Компонент1.GND, S1.Pin_1, S1.Pin_2, S2.Pin_1, S2.Pin_2, S3.Pin_1, S3.Pin_2, Q1.E, Part1.-, Display1.GND
  N1: Компонент1.D2, Part1.S
  N2: Компонент1.D3, R2.Pin_1
  N3: Компонент1.D4, S3.Pin_3, S3.Pin_4
  N4: Компонент1.D5, S1.Pin_3, S1.Pin_4
  N5: Компонент1.D6, S2.Pin_3, S2.Pin_4
  N6: Компонент1.D8, Part1.Vin
  5V: Компонент1.5V, Display1.VCC
  N7: Компонент1.A5, Display1.SCL
  N8: Компонент1.A4, Display1.SDA
  N9: Q1.B, R2.Pin_0
  N10: Q1.C, R1.Pin_1

custom parts:
  KY-022 Infrared Receiver Module: Arduino IR receiver module KY-022, reacts to 38kHz infrared light.
  LCD screen 16x2 IIC: LCD screen with HD44780 controller enables showing text, symbols, value or anything else that comes from Croduino/Arduino. It is capable of showing 16 symbols in two lines and therefore can be used in many projects that need to send clearly visible and legible output information.. • Color of symbols: White • Backlight: Blue • Dimensions: 80 x 36 x 12 mm • Screen dimensions: 64.5 x 16 mm •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
  Infrared LED - 5mm: A generic infrared LED (~1.2V)
